// Logisim project main.circ as structural Verilog: 10 circuits, main circuit TP34
module TP34 (
  output [2:0] out_1,
  output [2:0] out_2,
  output [2:0] out_3
);

  wire clk_out, disp0i_a_out, disp0i_b_out, disp0i_c_out, disp0i_d_out, disp0i_e_out, disp0i_f_out,
       disp0i_g_out, disp0i_p_out, disp1i_a_out, disp1i_b_out, disp1i_c_out, disp1i_d_out, disp1i_e_out,
       disp1i_f_out, disp1i_g_out, disp1i_p_out, disp2i_a_out, disp2i_b_out, disp2i_c_out, disp2i_d_out,
       disp2i_e_out, disp2i_f_out, disp2i_g_out, disp2i_p_out, reset_out, sevensegmentbase5driver_1_a,
       sevensegmentbase5driver_1_b, sevensegmentbase5driver_1_c, sevensegmentbase5driver_1_d,
       sevensegmentbase5driver_1_e, sevensegmentbase5driver_1_f, sevensegmentbase5driver_1_g,
       sevensegmentbase5driver_1_p, sevensegmentbase5driver_2_a, sevensegmentbase5driver_2_b,
       sevensegmentbase5driver_2_c, sevensegmentbase5driver_2_d, sevensegmentbase5driver_2_e,
       sevensegmentbase5driver_2_f, sevensegmentbase5driver_2_g, sevensegmentbase5driver_2_p,
       sevensegmentbase5driver_3_a, sevensegmentbase5driver_3_b, sevensegmentbase5driver_3_c,
       sevensegmentbase5driver_3_d, sevensegmentbase5driver_3_e, sevensegmentbase5driver_3_f,
       sevensegmentbase5driver_3_g, sevensegmentbase5driver_3_p;

  Button But ();  // open: out
  Clock clk (.out(clk_out));
  Button reset (.out(reset_out));
  base5counter125 base5counter125_1 (
    .counter(clk_out), .reset(reset_out), .out_4({out_1, out_2, out_3}));  // open: upDown, nextBlock
  sevenSegmentBase5Driver sevensegmentbase5driver_1 (
    .z(out_1[0]), .x(out_1[2]), .y(out_1[1]), .c(sevensegmentbase5driver_1_c),
    .d(sevensegmentbase5driver_1_d), .e(sevensegmentbase5driver_1_e), .f(sevensegmentbase5driver_1_f),
    .g(sevensegmentbase5driver_1_g), .p(sevensegmentbase5driver_1_p), .a(sevensegmentbase5driver_1_a),
    .b(sevensegmentbase5driver_1_b));
  sevenSegmentBase5Driver sevensegmentbase5driver_2 (
    .z(out_2[0]), .x(out_2[2]), .y(out_2[1]), .c(sevensegmentbase5driver_2_c),
    .d(sevensegmentbase5driver_2_d), .e(sevensegmentbase5driver_2_e), .f(sevensegmentbase5driver_2_f),
    .g(sevensegmentbase5driver_2_g), .p(sevensegmentbase5driver_2_p), .a(sevensegmentbase5driver_2_a),
    .b(sevensegmentbase5driver_2_b));
  sevenSegmentBase5Driver sevensegmentbase5driver_3 (
    .z(out_3[0]), .x(out_3[2]), .y(out_3[1]), .c(sevensegmentbase5driver_3_c),
    .d(sevensegmentbase5driver_3_d), .e(sevensegmentbase5driver_3_e), .f(sevensegmentbase5driver_3_f),
    .g(sevensegmentbase5driver_3_g), .p(sevensegmentbase5driver_3_p), .a(sevensegmentbase5driver_3_a),
    .b(sevensegmentbase5driver_3_b));
  disp_interface disp2i (
    .a_in(sevensegmentbase5driver_1_a), .b_in(sevensegmentbase5driver_1_b),
    .c_in(sevensegmentbase5driver_1_c), .d_in(sevensegmentbase5driver_1_d),
    .e_in(sevensegmentbase5driver_1_e), .f_in(sevensegmentbase5driver_1_f),
    .g_in(sevensegmentbase5driver_1_g), .p_in(sevensegmentbase5driver_1_p), .a_out(disp2i_a_out),
    .b_out(disp2i_b_out), .c_out(disp2i_c_out), .d_out(disp2i_d_out), .e_out(disp2i_e_out),
    .f_out(disp2i_f_out), .g_out(disp2i_g_out), .p_out(disp2i_p_out));
  disp_interface disp1i (
    .a_in(sevensegmentbase5driver_2_a), .b_in(sevensegmentbase5driver_2_b),
    .c_in(sevensegmentbase5driver_2_c), .d_in(sevensegmentbase5driver_2_d),
    .e_in(sevensegmentbase5driver_2_e), .f_in(sevensegmentbase5driver_2_f),
    .g_in(sevensegmentbase5driver_2_g), .p_in(sevensegmentbase5driver_2_p), .a_out(disp1i_a_out),
    .b_out(disp1i_b_out), .c_out(disp1i_c_out), .d_out(disp1i_d_out), .e_out(disp1i_e_out),
    .f_out(disp1i_f_out), .g_out(disp1i_g_out), .p_out(disp1i_p_out));
  disp_interface disp0i (
    .a_in(sevensegmentbase5driver_3_a), .b_in(sevensegmentbase5driver_3_b),
    .c_in(sevensegmentbase5driver_3_c), .d_in(sevensegmentbase5driver_3_d),
    .e_in(sevensegmentbase5driver_3_e), .f_in(sevensegmentbase5driver_3_f),
    .g_in(sevensegmentbase5driver_3_g), .p_in(sevensegmentbase5driver_3_p), .a_out(disp0i_a_out),
    .b_out(disp0i_b_out), .c_out(disp0i_c_out), .d_out(disp0i_d_out), .e_out(disp0i_e_out),
    .f_out(disp0i_f_out), .g_out(disp0i_g_out), .p_out(disp0i_p_out));
  _7_Segment_Display Disp2 (
    .g(disp2i_g_out), .f(disp2i_f_out), .a(disp2i_a_out), .b(disp2i_b_out), .e(disp2i_e_out),
    .d(disp2i_d_out), .c(disp2i_c_out), .dp(disp2i_p_out));
  _7_Segment_Display Disp1 (
    .g(disp1i_g_out), .f(disp1i_f_out), .a(disp1i_a_out), .b(disp1i_b_out), .e(disp1i_e_out),
    .d(disp1i_d_out), .c(disp1i_c_out), .dp(disp1i_p_out));
  _7_Segment_Display Disp0 (
    .g(disp0i_g_out), .f(disp0i_f_out), .a(disp0i_a_out), .b(disp0i_b_out), .e(disp0i_e_out),
    .d(disp0i_d_out), .c(disp0i_c_out), .dp(disp0i_p_out));
  LED Q22 (.in(out_1[2]));
  LED Q12 (.in(out_2[2]));
  LED Q02 (.in(out_3[2]));
  LED Q21 (.in(out_1[1]));
  LED Q11 (.in(out_2[1]));
  LED Q01 (.in(out_3[1]));
  LED Q20 (.in(out_1[0]));
  LED Q10 (.in(out_2[0]));
  LED Q00 (.in(out_3[0]));
endmodule

module disp_interface (
  input  a_in,
  input  b_in,
  input  c_in,
  input  d_in,
  input  e_in,
  input  f_in,
  input  g_in,
  input  p_in,
  output a_out,
  output b_out,
  output c_out,
  output d_out,
  output e_out,
  output f_out,
  output g_out,
  output p_out
);

  not not_1 (a_out, a_in);
  not not_2 (b_out, b_in);
  not not_3 (c_out, c_in);
  not not_4 (d_out, d_in);
  not not_5 (e_out, e_in);
  not not_6 (f_out, f_in);
  not not_7 (g_out, g_in);
  not not_8 (p_out, p_in);
endmodule

module sevenSegmentDefaultDriver (
  input  w,
  input  x,
  input  y,
  input  z,
  output a,
  output b,
  output c,
  output d,
  output e,
  output f,
  output g,
  output p
);

  wire and_1_out, and_2_out, and_3_out, and_4_out, and_5_out, and_6_out, and_7_out, and_8_out, and_9_out,
       and_10_out, and_11_out, and_12_out, and_13_out, and_14_out, and_15_out, and_16_out, and_17_out,
       and_18_out, and_19_out, and_20_out, and_21_out, and_22_out, and_23_out, and_24_out, and_25_out,
       and_26_out, and_27_out, and_28_out, and_29_out, and_30_out, and_31_out, and_32_out, and_33_out,
       and_34_out, and_35_out, and_36_out, and_37_out, and_38_out, and_39_out, and_40_out, not_1_out,
       not_2_out, not_3_out, not_4_out;

  not not_1 (not_1_out, w);
  not not_2 (not_2_out, x);
  not not_3 (not_3_out, y);
  not not_4 (not_4_out, z);
  and and_1 (and_1_out, not_2_out, not_4_out);
  and and_2 (and_2_out, not_1_out, y);
  and and_3 (and_3_out, not_1_out, x, z);
  and and_4 (and_4_out, w, not_2_out, not_3_out);
  and and_5 (and_5_out, w, not_4_out);
  and and_6 (and_6_out, x, y);
  and and_7 (and_7_out, not_1_out, not_3_out, not_4_out);
  and and_8 (and_8_out, not_1_out, y, z);
  and and_9 (and_9_out, not_2_out, not_4_out);
  and and_10 (and_10_out, w, not_3_out, z);
  and and_11 (and_11_out, not_1_out, not_2_out);
  and and_12 (and_12_out, not_1_out, x);
  and and_13 (and_13_out, w, not_2_out);
  and and_14 (and_14_out, not_3_out, z);
  and and_15 (and_15_out, not_1_out, not_3_out);
  and and_16 (and_16_out, not_1_out, z);
  and and_17 (and_17_out, x, not_3_out, z);
  and and_18 (and_18_out, not_1_out, not_2_out, not_4_out);
  and and_19 (and_19_out, not_1_out, not_2_out, y);
  and and_20 (and_20_out, not_1_out, y, not_4_out);
  and and_21 (and_21_out, not_2_out, not_3_out, not_4_out);
  and and_22 (and_22_out, w, not_3_out);
  and and_23 (and_23_out, not_2_out, y, z);
  and and_24 (and_24_out, x, y, not_4_out);
  and and_25 (and_25_out, not_2_out, not_4_out);
  and and_26 (and_26_out, y, not_4_out);
  and and_27 (and_27_out, w, y);
  and and_28 (and_28_out, w, x);
  and and_29 (and_29_out, not_3_out, not_4_out);
  and and_30 (and_30_out, not_1_out, x, not_3_out);
  and and_31 (and_31_out, x, not_4_out);
  and and_32 (and_32_out, w, not_2_out);
  and and_33 (and_33_out, w, y);
  and and_34 (and_34_out, not_2_out, y);
  and and_35 (and_35_out, w, not_2_out);
  and and_36 (and_36_out, not_1_out, x, not_3_out);
  and and_37 (and_37_out, not_1_out, x, not_4_out);
  and and_38 (and_38_out, x, not_3_out, z);
  and and_39 (and_39_out, y, not_4_out);
  and and_40 (and_40_out, w, z);
  or or_1 (a, and_1_out, and_2_out, and_3_out, and_4_out, and_5_out, and_6_out);
  or or_2 (b, and_7_out, and_8_out, and_9_out, and_10_out, and_11_out);
  or or_3 (c, and_12_out, and_13_out, and_14_out, and_15_out, and_16_out);
  or or_4 (d, and_17_out, and_18_out, and_19_out, and_20_out, and_21_out, and_22_out, and_23_out, and_24_out);
  or or_5 (e, and_25_out, and_26_out, and_27_out, and_28_out);
  or or_6 (f, and_29_out, and_30_out, and_31_out, and_32_out, and_33_out);
  or or_7 (g, and_34_out, and_35_out, and_36_out, and_37_out, and_38_out, and_39_out, and_40_out);

  assign p = 1'b0;
endmodule

module halfByteCounter (
  input  counter,
  input  reset,
  output [3:0] out_3,
  output nextBlock
);

  wire d_ff_1_qn, d_ff_2_qn, d_ff_3_qn;

  D_Flip_Flop d_ff_1 (.D(d_ff_1_qn), .clk(counter), .Q(out_3[0]), .Qn(d_ff_1_qn), .reset(reset));  // open: preset
  D_Flip_Flop d_ff_2 (.D(d_ff_2_qn), .clk(d_ff_1_qn), .Q(out_3[1]), .Qn(d_ff_2_qn), .reset(reset));  // open: preset
  D_Flip_Flop d_ff_3 (.D(d_ff_3_qn), .clk(d_ff_2_qn), .Q(out_3[2]), .Qn(d_ff_3_qn), .reset(reset));  // open: preset
  D_Flip_Flop d_ff_4 (.D(nextBlock), .clk(d_ff_3_qn), .Q(out_3[3]), .Qn(nextBlock), .reset(reset));  // open: preset
endmodule

module byteCounter (
  input  counter,
  input  reset,
  output [7:0] out_3,
  output nextBlock
);

  wire halfbytecounter_1_nextblock;

  halfByteCounter halfbytecounter_1 (
    .counter(counter), .reset(reset), .out_3(out_3[3:0]), .nextBlock(halfbytecounter_1_nextblock));
  halfByteCounter halfbytecounter_2 (
    .counter(halfbytecounter_1_nextblock), .reset(reset), .out_3(out_3[7:4]), .nextBlock(nextBlock));
endmodule

module base5counter (
  input  counter,
  input  reset,
  output [2:0] out_3,
  output nextBlock
);

  wire and_1_out, d_ff_1_qn, d_ff_2_qn, not_1_out, or_1_out;
  wire [2:0] d_ff_1_q;

  D_Flip_Flop d_ff_1 (.D(d_ff_1_qn), .clk(counter), .Q(d_ff_1_q[0]), .Qn(d_ff_1_qn), .reset(or_1_out));  // open: preset
  or or_1 (or_1_out, reset, and_1_out);
  D_Flip_Flop d_ff_2 (
    .D(d_ff_2_qn), .clk(d_ff_1_qn), .Q(d_ff_1_q[1]), .Qn(d_ff_2_qn), .reset(or_1_out));  // open: preset
  and and_1 (and_1_out, d_ff_1_q[0], not_1_out, d_ff_1_q[2]);
  D_Flip_Flop d_ff_3 (
    .D(nextBlock), .clk(d_ff_2_qn), .Q(d_ff_1_q[2]), .Qn(nextBlock), .reset(or_1_out));  // open: preset
  not not_1 (not_1_out, d_ff_1_q[1]);
  binaryToBase5 binarytobase5_1 (.in_1(d_ff_1_q), .value(out_3));

  // Notes on the sheet:
  //   Convert basic hex signal to given table
endmodule

module base5counter125 (
  input  upDown,
  input  counter,
  input  reset,
  output [8:0] out_4,
  output nextBlock
);

  wire and_1_out, and_2_out, base5counter_1_nextblock, base5counter_2_nextblock, not_1_out, not_2_out,
       undriven;

  not not_1 (not_1_out, upDown);
  not not_2 (not_2_out, not_1_out);
  and and_1 (and_1_out, counter, not_1_out);
  and and_2 (and_2_out, not_2_out, undriven);
  base5counter base5counter_1 (
    .counter(and_1_out), .reset(reset), .out_3(out_4[2:0]), .nextBlock(base5counter_1_nextblock));
  base5counterDown base5counterdown_1 (.counter(and_2_out));  // open: reset, value, nextBlock
  base5counterDown base5counterdown_2 ();  // open: counter, reset, value, nextBlock
  base5counter base5counter_2 (
    .counter(base5counter_1_nextblock), .reset(reset), .out_3(out_4[5:3]),
    .nextBlock(base5counter_2_nextblock));
  base5counterDown base5counterdown_3 ();  // open: counter, reset, value, nextBlock
  base5counter base5counter_3 (
    .counter(base5counter_2_nextblock), .reset(reset), .out_3(out_4[8:6]), .nextBlock(nextBlock));
  base5counterDown base5counterdown_4 ();  // open: counter, reset, value, nextBlock

  // Notes on the sheet:
  //   0 = down 
  //   1 = up
endmodule

module sevenSegmentBase5Driver (
  input  x,
  input  y,
  input  z,
  output a,
  output b,
  output c,
  output d,
  output e,
  output f,
  output g,
  output p
);

  wire and_1_out, and_2_out, and_3_out, not_1_out, not_2_out;

  not not_1 (not_1_out, x);
  not not_2 (not_2_out, y);
  not not_3 (f, z);
  or or_1 (a, not_1_out, y);
  or or_2 (c, not_2_out, not_1_out);
  or or_3 (d, not_1_out, y);
  and and_1 (and_1_out, not_1_out, not_2_out);
  and and_2 (and_2_out, not_2_out, f);
  or or_4 (g, and_1_out, and_2_out, and_3_out);
  and and_3 (and_3_out, y, z);

  assign b = 1'b1;
  assign e = y;
  assign p = 1'b0;
endmodule

module binaryToBase5 (
  input  [2:0] in_1,
  output [2:0] value
);

  wire and_1_out, and_2_out, not_1_out, not_2_out, not_3_out;

  not not_1 (not_1_out, in_1[2]);
  not not_2 (not_2_out, in_1[1]);
  not not_3 (not_3_out, in_1[0]);
  and and_1 (and_1_out, not_2_out, in_1[0]);
  and and_2 (and_2_out, in_1[1], not_3_out);
  and and_3 (value[1], not_1_out, not_3_out);
  or or_1 (value[0], in_1[0], in_1[1]);
  or or_2 (value[2], and_1_out, and_2_out, in_1[2]);
endmodule

module base5counterDown (
  input  counter,
  input  reset,
  output [2:0] value,
  output nextBlock
);

  wire and_1_out, and_2_out, and_3_out, button_1_out, d_ff_1_qn, d_ff_2_q, d_ff_3_qn, d_ff_4_qn, or_1_out,
       or_2_out, or_3_out, t_ff_1_qn, t_ff_2_qn, undriven, undriven_2, undriven_3, undriven_4;
  wire [2:0] d_ff_1_q, t_ff_1_q;

  or or_1 (or_1_out, t_ff_1_q[2], t_ff_1_q[1], t_ff_1_q[0]);
  D_Flip_Flop d_ff_1 (
    .D(d_ff_1_qn), .clk(undriven_2), .Q(d_ff_1_q[0]), .Qn(d_ff_1_qn), .preset(undriven_3), .reset(or_2_out));
  or or_2 (or_2_out, undriven, and_2_out);
  T_Flip_Flop t_ff_1 (.T(or_1_out), .clk(counter), .Q(t_ff_1_q[0]), .Qn(t_ff_1_qn), .reset(reset));  // open: preset
  D_Flip_Flop d_ff_2 (.Q(d_ff_2_q), .preset(and_2_out), .reset(button_1_out));  // open: D, clk, Qn
  LED led_1 (.in(d_ff_2_q));
  Button button_1 (.out(button_1_out));
  and and_1 (and_1_out, t_ff_1_q[1], t_ff_1_qn);
  D_Flip_Flop d_ff_3 (
    .D(d_ff_3_qn), .clk(d_ff_1_q[0]), .Q(d_ff_1_q[1]), .Qn(d_ff_3_qn), .preset(undriven_4), .reset(or_2_out));
  and and_2 (and_2_out, d_ff_1_q[0], d_ff_1_q[1], d_ff_1_q[2]);
  T_Flip_Flop t_ff_2 (.T(or_3_out), .clk(counter), .Q(t_ff_1_q[1]), .Qn(t_ff_2_qn), .reset(reset));  // open: preset
  or or_3 (or_3_out, t_ff_1_q[2], and_1_out);
  D_Flip_Flop d_ff_4 (
    .D(d_ff_4_qn), .clk(d_ff_1_q[1]), .Q(d_ff_1_q[2]), .Qn(d_ff_4_qn), .preset(or_2_out));  // open: reset
  T_Flip_Flop t_ff_3 (.T(and_3_out), .clk(counter), .Q(t_ff_1_q[2]), .reset(reset));  // open: Qn, preset
  and and_3 (and_3_out, t_ff_1_qn, t_ff_2_qn);
  binaryToBase5 binarytobase5_1 (.in_1(t_ff_1_q), .value(value));

  // Notes on the sheet:
  //   Ici on a un problème de valeurs qui pop up très rapidement comme montré avec le s-latch et qui casse donc notre circuit
  //   Convert basic hex signal to given table
endmodule
