// Logisim project tp34.circ as structural Verilog: 8 circuits, main circuit TP34
module TP34 (
);

  wire But_out, clk_out, disp0i_a_out, disp0i_b_out, disp0i_c_out, disp0i_d_out, disp0i_e_out, disp0i_f_out,
       disp0i_g_out, disp0i_p_out, disp1i_a_out, disp1i_b_out, disp1i_c_out, disp1i_d_out, disp1i_e_out,
       disp1i_f_out, disp1i_g_out, disp1i_p_out, disp2i_a_out, disp2i_b_out, disp2i_c_out, disp2i_d_out,
       disp2i_e_out, disp2i_f_out, disp2i_g_out, disp2i_p_out, goalvalue_1_upordowncurrent, reset_out,
       sevensegmentdriver_1_a, sevensegmentdriver_1_b, sevensegmentdriver_1_c, sevensegmentdriver_1_d,
       sevensegmentdriver_1_e, sevensegmentdriver_1_f, sevensegmentdriver_1_g, sevensegmentdriver_1_p,
       sevensegmentdriver_2_a, sevensegmentdriver_2_b, sevensegmentdriver_2_c, sevensegmentdriver_2_d,
       sevensegmentdriver_2_e, sevensegmentdriver_2_f, sevensegmentdriver_2_g, sevensegmentdriver_2_p,
       sevensegmentdriver_3_a, sevensegmentdriver_3_b, sevensegmentdriver_3_c, sevensegmentdriver_3_d,
       sevensegmentdriver_3_e, sevensegmentdriver_3_f, sevensegmentdriver_3_g, sevensegmentdriver_3_p;
  wire [8:0] base5counter_1_lsn;

  Button But (.out(But_out));
  Clock clk (.out(clk_out));
  Button reset (.out(reset_out));
  goalValue goalvalue_1 (
    .value(base5counter_1_lsn), .button(But_out), .reset(reset_out), .upOrDownDefault(1'b0),
    .upOrDownCurrent(goalvalue_1_upordowncurrent));
  base5Counter base5counter_1 (
    .clock(clk_out), .reset(reset_out), .upDown(goalvalue_1_upordowncurrent), .MSN(base5counter_1_lsn[8:6]),
    .LSN(base5counter_1_lsn[2:0]), .MN(base5counter_1_lsn[5:3]));
  sevenSegmentDriver sevensegmentdriver_1 (
    .value(base5counter_1_lsn[8:6]), .b(sevensegmentdriver_1_b), .c(sevensegmentdriver_1_c),
    .d(sevensegmentdriver_1_d), .e(sevensegmentdriver_1_e), .f(sevensegmentdriver_1_f),
    .g(sevensegmentdriver_1_g), .p(sevensegmentdriver_1_p), .a(sevensegmentdriver_1_a));
  sevenSegmentDriver sevensegmentdriver_2 (
    .value(base5counter_1_lsn[5:3]), .b(sevensegmentdriver_2_b), .c(sevensegmentdriver_2_c),
    .d(sevensegmentdriver_2_d), .e(sevensegmentdriver_2_e), .f(sevensegmentdriver_2_f),
    .g(sevensegmentdriver_2_g), .p(sevensegmentdriver_2_p), .a(sevensegmentdriver_2_a));
  sevenSegmentDriver sevensegmentdriver_3 (
    .value(base5counter_1_lsn[2:0]), .b(sevensegmentdriver_3_b), .c(sevensegmentdriver_3_c),
    .d(sevensegmentdriver_3_d), .e(sevensegmentdriver_3_e), .f(sevensegmentdriver_3_f),
    .g(sevensegmentdriver_3_g), .p(sevensegmentdriver_3_p), .a(sevensegmentdriver_3_a));
  disp_interface disp2i (
    .a_in(sevensegmentdriver_1_a), .b_in(sevensegmentdriver_1_b), .c_in(sevensegmentdriver_1_c),
    .d_in(sevensegmentdriver_1_d), .e_in(sevensegmentdriver_1_e), .f_in(sevensegmentdriver_1_f),
    .g_in(sevensegmentdriver_1_g), .p_in(sevensegmentdriver_1_p), .a_out(disp2i_a_out), .b_out(disp2i_b_out),
    .c_out(disp2i_c_out), .d_out(disp2i_d_out), .e_out(disp2i_e_out), .f_out(disp2i_f_out),
    .g_out(disp2i_g_out), .p_out(disp2i_p_out));
  disp_interface disp1i (
    .a_in(sevensegmentdriver_2_a), .b_in(sevensegmentdriver_2_b), .c_in(sevensegmentdriver_2_c),
    .d_in(sevensegmentdriver_2_d), .e_in(sevensegmentdriver_2_e), .f_in(sevensegmentdriver_2_f),
    .g_in(sevensegmentdriver_2_g), .p_in(sevensegmentdriver_2_p), .a_out(disp1i_a_out), .b_out(disp1i_b_out),
    .c_out(disp1i_c_out), .d_out(disp1i_d_out), .e_out(disp1i_e_out), .f_out(disp1i_f_out),
    .g_out(disp1i_g_out), .p_out(disp1i_p_out));
  disp_interface disp0i (
    .a_in(sevensegmentdriver_3_a), .b_in(sevensegmentdriver_3_b), .c_in(sevensegmentdriver_3_c),
    .d_in(sevensegmentdriver_3_d), .e_in(sevensegmentdriver_3_e), .f_in(sevensegmentdriver_3_f),
    .g_in(sevensegmentdriver_3_g), .p_in(sevensegmentdriver_3_p), .a_out(disp0i_a_out), .b_out(disp0i_b_out),
    .c_out(disp0i_c_out), .d_out(disp0i_d_out), .e_out(disp0i_e_out), .f_out(disp0i_f_out),
    .g_out(disp0i_g_out), .p_out(disp0i_p_out));
  _7_Segment_Display Disp2 (
    .g(disp2i_g_out), .f(disp2i_f_out), .a(disp2i_a_out), .b(disp2i_b_out), .e(disp2i_e_out),
    .d(disp2i_d_out), .c(disp2i_c_out), .dp(disp2i_p_out));
  _7_Segment_Display Disp1 (
    .g(disp1i_g_out), .f(disp1i_f_out), .a(disp1i_a_out), .b(disp1i_b_out), .e(disp1i_e_out),
    .d(disp1i_d_out), .c(disp1i_c_out), .dp(disp1i_p_out));
  _7_Segment_Display Disp0 (
    .g(disp0i_g_out), .f(disp0i_f_out), .a(disp0i_a_out), .b(disp0i_b_out), .e(disp0i_e_out),
    .d(disp0i_d_out), .c(disp0i_c_out), .dp(disp0i_p_out));
  LED Q22 (.in(base5counter_1_lsn[8]));
  LED Q12 (.in(base5counter_1_lsn[5]));
  LED Q02 (.in(base5counter_1_lsn[2]));
  LED Q21 (.in(base5counter_1_lsn[7]));
  LED Q11 (.in(base5counter_1_lsn[4]));
  LED Q01 (.in(base5counter_1_lsn[1]));
  LED Q20 (.in(base5counter_1_lsn[6]));
  LED Q10 (.in(base5counter_1_lsn[3]));
  LED Q00 (.in(base5counter_1_lsn[0]));
endmodule

module base5Counter (
  input  upDown,
  input  clock,
  input  reset,
  output [2:0] LSN,
  output [2:0] MN,
  output [2:0] MSN
);

  wire and_1_out, clockfive_1_carryout, clockfive_2_carryout, clockfive_3_carryout;
  wire [2:0] clockfive_1_nextvalue, clockfive_2_nextvalue, clockfive_3_nextvalue;

  clockFive clockfive_1 (
    .upDown(upDown), .carry(1'b1), .value(LSN), .nextValue(clockfive_1_nextvalue),
    .carryOut(clockfive_1_carryout));
  threeBitMemory threebitmemory_1 (
    .change(clockfive_1_nextvalue), .reset(reset), .clock(clock), .resetValues(3'b010), .memory(LSN));
  clockFive clockfive_2 (
    .upDown(upDown), .carry(clockfive_1_carryout), .value(MN), .nextValue(clockfive_2_nextvalue),
    .carryOut(clockfive_2_carryout));
  threeBitMemory threebitmemory_2 (
    .change(clockfive_2_nextvalue), .reset(reset), .clock(clock), .resetValues(3'b001), .memory(MN));
  and and_1 (and_1_out, clockfive_1_carryout, clockfive_2_carryout);
  clockFive clockfive_3 (
    .upDown(upDown), .carry(and_1_out), .value(MSN), .nextValue(clockfive_3_nextvalue),
    .carryOut(clockfive_3_carryout));
  threeBitMemory threebitmemory_3 (
    .change(clockfive_3_nextvalue), .reset(reset), .clock(clock), .resetValues(3'b101), .memory(MSN));
endmodule

module threeBitMemory (
  input  [2:0] change,
  input  reset,
  input  clock,
  input  [2:0] resetValues,
  output [2:0] memory
);

  wire and_1_out, and_2_out, and_3_out, and_4_out, and_5_out, and_6_out, xor_1_out, xor_2_out, xor_3_out;

  D_Flip_Flop d_ff_1 (.D(change[2]), .clk(clock), .Q(memory[2]), .preset(and_1_out), .reset(and_2_out));  // open: Qn
  and and_1 (and_1_out, reset, resetValues[2]);
  and and_2 (and_2_out, reset, xor_1_out);
  xor xor_1 (xor_1_out, 1'b1, resetValues[2]);
  and and_3 (and_3_out, reset, resetValues[1]);
  D_Flip_Flop d_ff_2 (.D(change[1]), .clk(clock), .Q(memory[1]), .preset(and_3_out), .reset(and_4_out));  // open: Qn
  and and_4 (and_4_out, reset, xor_2_out);
  xor xor_2 (xor_2_out, 1'b1, resetValues[1]);
  and and_5 (and_5_out, reset, resetValues[0]);
  D_Flip_Flop d_ff_3 (.D(change[0]), .clk(clock), .Q(memory[0]), .preset(and_5_out), .reset(and_6_out));  // open: Qn
  and and_6 (and_6_out, reset, xor_3_out);
  xor xor_3 (xor_3_out, 1'b1, resetValues[0]);
endmodule

module goalValue (
  input  [8:0] value,
  input  button,
  input  reset,
  input  upOrDownDefault,
  output upOrDownCurrent
);

  wire and_1_out, and_2_out, and_3_out, d_ff_1_q, latch_1_out_3, not_1_out, or_1_out;
  wire [8:0] not_2_out, xor_1_out;

  D_Flip_Flop d_ff_1 (.Q(d_ff_1_q), .preset(and_1_out), .reset(or_1_out));  // open: D, clk, Qn
  assign xor_1_out = value ^ 9'h139;  // XOR_Gate xor_1, 9 bits wide
  not not_1 (not_1_out, and_2_out);
  and and_1 (and_1_out, button, not_1_out);
  or or_1 (or_1_out, reset, and_3_out);
  assign not_2_out = ~xor_1_out;  // NOT_Gate not_2, 9 bits wide
  and and_2 (and_2_out, not_2_out[8], not_2_out[7], not_2_out[6], not_2_out[5], not_2_out[4], not_2_out[3], not_2_out[2], not_2_out[1], not_2_out[0]);
  and and_3 (and_3_out, d_ff_1_q, and_2_out);
  xor xor_2 (upOrDownCurrent, latch_1_out_3, upOrDownDefault);
  latch latch_1 (.button(and_3_out), .reset(reset), .out_3(latch_1_out_3));

  // Notes on the sheet:
  //   Checks if value is 423 base 5
  //   If the button is pressed when value is 423 do nothing
  //   If value is 423 and button has already been pressed change direction and store it
endmodule

module clockFive (
  input  upDown,
  input  carry,
  input  [2:0] value,
  output [2:0] nextValue,
  output carryOut
);

  wire and_1_out, and_2_out, and_3_out, and_4_out, and_5_out, and_6_out, and_7_out, and_8_out, and_9_out,
       and_10_out, and_11_out, and_12_out, and_13_out, and_14_out, and_15_out, not_1_out, not_2_out,
       not_3_out, not_4_out, not_5_out;

  not not_1 (not_1_out, upDown);
  not not_2 (not_2_out, carry);
  not not_3 (not_3_out, value[2]);
  not not_4 (not_4_out, value[1]);
  not not_5 (not_5_out, value[0]);
  and and_1 (and_1_out, not_2_out, value[2]);
  and and_2 (and_2_out, carry, not_3_out);
  and and_3 (and_3_out, not_1_out, value[2], not_4_out, value[0]);
  and and_4 (and_4_out, upDown, value[2], value[1]);
  and and_5 (and_5_out, not_2_out, value[1]);
  and and_6 (and_6_out, upDown, carry, not_4_out, value[0]);
  and and_7 (and_7_out, not_1_out, carry, value[2], not_4_out);
  and and_8 (and_8_out, not_2_out, value[0]);
  and and_9 (and_9_out, not_1_out, value[2], value[0]);
  and and_10 (and_10_out, not_1_out, carry, not_3_out, not_5_out);
  and and_11 (and_11_out, upDown, carry, not_3_out, not_4_out);
  and and_12 (and_12_out, upDown, carry, not_4_out, not_5_out);
  and and_13 (and_13_out, carry, value[2], value[1]);
  and and_14 (and_14_out, upDown, carry, not_3_out, value[1], not_5_out);
  and and_15 (and_15_out, not_1_out, carry, value[2], not_4_out, not_5_out);
  or or_1 (nextValue[2], and_1_out, and_2_out, and_3_out, and_4_out);
  or or_2 (nextValue[1], and_5_out, and_6_out, and_7_out);
  or or_3 (nextValue[0], and_8_out, and_9_out, and_10_out, and_11_out, and_12_out, and_13_out);
  or or_4 (carryOut, and_14_out, and_15_out);
endmodule

module sevenSegmentDriver (
  input  [2:0] value,
  output a,
  output b,
  output c,
  output d,
  output e,
  output f,
  output g,
  output p
);

  wire and_1_out, and_2_out, and_3_out, and_4_out, and_5_out, and_6_out, and_7_out, not_1_out, not_2_out;

  not not_1 (not_1_out, value[2]);
  not not_2 (not_2_out, value[1]);
  not not_3 (f, value[0]);
  or or_1 (a, not_1_out, value[1]);
  or or_2 (b, value[0], value[1], value[2]);
  and and_1 (and_1_out, not_1_out, value[1]);
  and and_2 (and_2_out, value[2], not_2_out);
  and and_3 (and_3_out, not_1_out, value[0]);
  or or_3 (d, not_1_out, value[1]);
  and and_4 (and_4_out, not_1_out, f);
  and and_5 (and_5_out, not_2_out, f);
  and and_6 (and_6_out, value[1], value[0]);
  and and_7 (and_7_out, not_1_out, not_2_out);
  or or_4 (c, and_1_out, and_2_out, and_3_out);
  or or_5 (e, and_4_out, value[1]);
  or or_6 (g, and_5_out, and_6_out, and_7_out);

  assign p = 1'b0;
endmodule

module latch (
  input  button,
  input  reset,
  output out_3
);

  wire not_1_out;

  not not_1 (not_1_out, out_3);
  D_Flip_Flop d_ff_1 (.D(not_1_out), .clk(button), .Q(out_3), .reset(reset));  // open: Qn, preset
endmodule

module disp_interface (
  input  a_in,
  input  b_in,
  input  c_in,
  input  d_in,
  input  e_in,
  input  f_in,
  input  g_in,
  input  p_in,
  output a_out,
  output b_out,
  output c_out,
  output d_out,
  output e_out,
  output f_out,
  output g_out,
  output p_out
);

  not not_1 (a_out, a_in);
  not not_2 (b_out, b_in);
  not not_3 (c_out, c_in);
  not not_4 (d_out, d_in);
  not not_5 (e_out, e_in);
  not not_6 (f_out, f_in);
  not not_7 (g_out, g_in);
  not not_8 (p_out, p_in);
endmodule
